# Fritzing sketch Cicruit_Diagramm (saved by Fritzing 1.0.4)

parts:
  M1 = DC Motor [voltage_(max)=24V voltage_(min)=14]
  Mod1 = Raspberry Pi 4B
  ANT1 = Antenna
  Ant = TEST-POINT [package=pad.02x.02]
  VCC = TEST-POINT [package=pad.02x.02]
  GND = TEST-POINT [package=pad.02x.02]
  TP1 = TEST-POINT [package=pad.02x.02]
  TP2 = TEST-POINT [package=pad.02x.02]
  TP3 = TEST-POINT [package=pad.02x.02]
  TP4 = TEST-POINT [package=pad.02x.02]
  U1 = Sharp PC847X [package=THT]
  IC1 = A4950 [package=soicn]
  U3 = RELAY [package=relay-t9a]
  Endschalter_Tor_Komplett_Offen = Toggle Switch [package=THT]
  Endschalter_Tor_Komplett_geschlossen = Toggle Switch [package=THT]
  Warn_Lampe = LED - 5mm [color="White (8000K)" current=1A package="5 mm [THT]"]
  TP5 = TEST-POINT [package=pad.02x.02]
  TP6 = TEST-POINT [package=pad.02x.02]
  TP7 = TEST-POINT [package=pad.02x.02]
  TP8 = TEST-POINT [package=pad.02x.02]
  TP9 = TEST-POINT [package=pad.02x.02]
  TP10 = TEST-POINT [package=pad.02x.02]
  U4 = RELAY [package=relay-t9a]

nets:
  N1: M1.pin_1, IC1.OUT2
  N2: M1.pin_2, IC1.OUT1
  N3: Mod1.3V3, TP1.1, TP2.1, U1.Pin_12, U1.Pin_14, U1.Pin_16
  N4: Mod1.5V, U4.NC
  N5: Mod1.GPIO3, TP4.1
  N6: Mod1.GPIO4, TP3.1
  N7: Mod1.GPIO14, IC1.IN2
  N8: Mod1.GPIO15, U4.COIL1
  N9: Mod1.GPIO17, U1.Pin_15
  N10: Mod1.GPIO18, U3.COIL1
  N11: Mod1.GPIO27, U1.Pin_13
  N12: Mod1.GPIO22, U1.Pin_11
  N13: ANT1.antenna_lead, Ant.1
  24V: VCC.1, IC1.VBB, U3.MAIN, Endschalter_Tor_Komplett_Offen.COM, Endschalter_Tor_Komplett_geschlossen.COM, TP6.1, TP7.1
  0V: GND.1, U1.Pin_2, U1.Pin_4, U1.Pin_6, IC1.GND, IC1.VREF, U3.COIL2, Warn_Lampe.cathode, TP8.1, TP9.1, TP10.1, U4.COIL2, U4.NO
  N14: U1.Pin_1, TP5.1
  N15: U1.Pin_3, Endschalter_Tor_Komplett_Offen.L1
  N16: U1.Pin_5, Endschalter_Tor_Komplett_geschlossen.L1
  N17: IC1.IN1, U4.MAIN
  N18: U3.NO, Warn_Lampe.anode

notes:
  Raspberry PI ca. 50€
  2ch RF Empfänger ca. 20€
  Optokoppler ca. 5€
  DC PWM Motorsteuerung ca. 25€
  Relais ca. 5€
  Lichtschranke
